# Fritzing sketch ESP01_Arduino_Blynk (saved by Fritzing 0.9.3b)
breadboards: 1

parts:
  Part1 = Arduino Uno (Rev3)
  Espessif_Serial_Wifi_Modul_1 = ESP8266 ESP01 [part_number=ESP8266 package=THT]
  LED2 = LED - 3mm [color="Red (633nm)" package="3 mm [THT]"]
  S1 = Momentary Switch [package=ksa_sealed_tac_switch]

nets:
  N1: Part1.D0/RX, Espessif_Serial_Wifi_Modul_1.RXD
  N2: Part1.D1/TX, Espessif_Serial_Wifi_Modul_1.TXD
  GND: Part1.GND, Espessif_Serial_Wifi_Modul_1.GND, LED2.cathode, S1.4
  N3: Espessif_Serial_Wifi_Modul_1.VCC, Espessif_Serial_Wifi_Modul_1.CH_PD
  N4: Espessif_Serial_Wifi_Modul_1.GPIO16, S1.1
  N5: Espessif_Serial_Wifi_Modul_1.GPIO00, LED2.anode

notes:
  pada bagian vcc sudah di jumper/ penggabungan pin 3.3v & ch_pd pada esp 01.
  Pada saat upload program tekan buuton reset yang terhubung ke rst esp-01.
  Setting board = Arduino Uno

custom parts:
  ESP8266 ESP01: Generic WiFi Module based on the ESP8266 with onboard PCB antenna and UART communications

// code stored in the sketch: Esp01_arduino_blynk_code.ino
//https://create.arduino.cc/projecthub/pratikdesai/how-to-program-esp8266-esp-01-module-with-arduino-uno-598166

#define BLYNK_PRINT Serial
#include <ESP8266_Lib.h> //https://github.com/vshymanskyy/BlynkESP8266
#include <BlynkSimpleShieldEsp8266.h>
#include <SoftwareSerial.h>
#define ESP8266_BAUD 9600

char auth[] = "0ozhi5RHI7eHNHtlWY3lFKOO4mawQFYv";//Drop your blynk token
char ssid[] = "Redmi"; //You can replace the wifi name to your wifi 
char pass[] = "123123123";  //Type password of your wifi.

SoftwareSerial EspSerial(2, 3); // RX, TX
WidgetLCD lcd(V0);

ESP8266 wifi(&EspSerial);

void setup()
{

  Serial.begin(9600);
  EspSerial.begin(ESP8266_BAUD);
  Blynk.begin(auth, wifi, ssid, pass);
   lcd.clear();
 lcd.print(1, 1, "IoT");
}

void loop()
{
  Blynk.run();
}
